// Logisim project дз1.circ as structural Verilog: 2 circuits, main circuit МКНФ
module \МКНФ  (
);

  wire and_1_out, and_2_out, and_3_out, not_1_out, not_2_out, not_3_out, not_4_out, or_1_out, or_2_out,
       or_3_out, or_4_out, or_5_out, or_6_out, or_7_out, x0_out, x1_out, x2_out, x3_out;

  Clock x0 (.out(x0_out));
  Clock x1 (.out(x1_out));
  Clock x2 (.out(x2_out));
  Clock x3 (.out(x3_out));
  or or_1 (or_1_out, x3_out, x2_out);
  not not_1 (not_1_out, x2_out);
  or or_2 (or_2_out, x3_out, not_2_out);
  not not_2 (not_2_out, x2_out);
  not not_3 (not_3_out, x0_out);
  or or_3 (or_3_out, x2_out, not_4_out);
  not not_4 (not_4_out, x1_out);
  or or_4 (or_4_out, or_1_out, x0_out);
  or or_5 (or_5_out, not_1_out, x1_out);
  or or_6 (or_6_out, or_2_out, not_3_out);
  or or_7 (or_7_out, or_3_out, x0_out);
  and and_1 (and_1_out, or_4_out, or_5_out);
  and and_2 (and_2_out, or_6_out, or_7_out);
  and and_3 (and_3_out, and_1_out, and_2_out);
  LED led_1 (.in(and_3_out));
endmodule

module \СДНФ  (
);

  wire and_1_out, and_2_out, and_3_out, and_4_out, and_5_out, and_6_out, and_7_out, and_8_out, and_9_out,
       and_10_out, and_11_out, and_12_out, and_13_out, and_14_out, and_15_out, and_16_out, and_17_out,
       and_18_out, and_19_out, and_20_out, and_21_out, and_22_out, and_23_out, and_24_out, not_1_out,
       not_2_out, not_3_out, not_4_out, not_5_out, not_6_out, not_7_out, not_8_out, not_9_out, not_10_out,
       not_11_out, not_12_out, not_13_out, not_14_out, or_1_out, or_2_out, or_3_out, or_4_out, or_5_out,
       or_6_out, or_7_out, x0_out, x1_out, x2_out, x3_out;

  Clock x0 (.out(x0_out));
  Clock x1 (.out(x1_out));
  Clock x2 (.out(x2_out));
  Clock x3 (.out(x3_out));
  not not_1 (not_1_out, x3_out);
  and and_1 (and_1_out, not_1_out, not_2_out);
  not not_2 (not_2_out, x2_out);
  not not_3 (not_3_out, x1_out);
  and and_2 (and_2_out, not_3_out, x0_out);
  not not_4 (not_4_out, x3_out);
  and and_3 (and_3_out, not_4_out, not_5_out);
  not not_5 (not_5_out, x2_out);
  and and_4 (and_4_out, x1_out, x0_out);
  not not_6 (not_6_out, x3_out);
  and and_5 (and_5_out, not_6_out, x2_out);
  and and_6 (and_6_out, x1_out, not_7_out);
  not not_7 (not_7_out, x0_out);
  and and_7 (and_7_out, x3_out, not_8_out);
  not not_8 (not_8_out, x2_out);
  not not_9 (not_9_out, x1_out);
  and and_8 (and_8_out, not_9_out, not_10_out);
  not not_10 (not_10_out, x0_out);
  and and_9 (and_9_out, x3_out, not_11_out);
  not not_11 (not_11_out, x2_out);
  not not_12 (not_12_out, x1_out);
  and and_10 (and_10_out, not_12_out, x0_out);
  and and_11 (and_11_out, x3_out, not_13_out);
  not not_13 (not_13_out, x2_out);
  and and_12 (and_12_out, x1_out, x0_out);
  and and_13 (and_13_out, x3_out, x2_out);
  and and_14 (and_14_out, x1_out, not_14_out);
  not not_14 (not_14_out, x0_out);
  and and_15 (and_15_out, x3_out, x2_out);
  and and_16 (and_16_out, x1_out, x0_out);
  and and_17 (and_17_out, and_1_out, and_2_out);
  and and_18 (and_18_out, and_3_out, and_4_out);
  and and_19 (and_19_out, and_5_out, and_6_out);
  and and_20 (and_20_out, and_7_out, and_8_out);
  and and_21 (and_21_out, and_9_out, and_10_out);
  and and_22 (and_22_out, and_11_out, and_12_out);
  and and_23 (and_23_out, and_13_out, and_14_out);
  and and_24 (and_24_out, and_15_out, and_16_out);
  or or_1 (or_1_out, and_17_out, and_18_out);
  or or_2 (or_2_out, and_19_out, and_20_out);
  or or_3 (or_3_out, and_21_out, and_22_out);
  or or_4 (or_4_out, and_23_out, and_24_out);
  or or_5 (or_5_out, or_1_out, or_2_out);
  or or_6 (or_6_out, or_3_out, or_4_out);
  or or_7 (or_7_out, or_5_out, or_6_out);
  LED led_1 (.in(or_7_out));
endmodule
