// Logisim project дз 2.circ as structural Verilog: 9 circuits, main circuit RS_trigger
module RS_trigger (
  input  R,
  input  C,
  input  S,
  input  reset_0,
  input  reset_1,
  output Q,
  output NQ
);

  wire and_1_out, and_2_out, and_3_out, and_4_out, not_1_out, not_2_out, or_1_out, or_2_out;

  and and_1 (and_1_out, R, C);
  and and_2 (and_2_out, C, S);
  not not_1 (not_1_out, reset_0);
  or or_1 (or_1_out, and_1_out, reset_0);
  and and_3 (and_3_out, and_2_out, not_1_out);
  not not_2 (not_2_out, reset_1);
  and and_4 (and_4_out, or_1_out, not_2_out);
  or or_2 (or_2_out, and_3_out, reset_1);
  nor nor_1 (Q, and_4_out, NQ);
  nor nor_2 (NQ, Q, or_2_out);
endmodule

module JK_trigger (
  input  J,
  input  C,
  input  K,
  input  reset_0,
  input  reset_1,
  output Q,
  output NQ
);

  wire and_1_out, and_2_out, not_1_out, rs_trigger_1_nq, rs_trigger_1_q;

  and and_1 (and_1_out, NQ, J);
  and and_2 (and_2_out, K, Q);
  RS_trigger rs_trigger_1 (
    .R(and_1_out), .C(C), .S(and_2_out), .reset_0(reset_1), .reset_1(reset_0), .Q(rs_trigger_1_q),
    .NQ(rs_trigger_1_nq));
  not not_1 (not_1_out, C);
  RS_trigger rs_trigger_2 (
    .R(rs_trigger_1_q), .C(not_1_out), .S(rs_trigger_1_nq), .reset_0(reset_0), .reset_1(reset_1), .Q(Q),
    .NQ(NQ));
endmodule

module T_trigger (
  input  T,
  input  C,
  input  reset_0,
  input  reset_1,
  output Q,
  output NQ
);

  JK_trigger jk_trigger_1 (.J(T), .C(C), .K(T), .reset_0(reset_0), .reset_1(reset_1), .Q(Q), .NQ(NQ));
endmodule

module SyncDecreaseCounter (
  input  reset,
  output x0,
  output x1,
  output x2,
  output x3
);

  wire and_1_out, and_2_out, and_3_out, and_4_out, and_5_out, and_6_out, C_out, not_1_out, not_2_out,
       not_3_out, not_4_out, not_5_out, not_6_out, or_1_out;

  Clock C (.out(C_out));
  and and_1 (and_1_out, reset, not_1_out);
  not not_1 (not_1_out, and_2_out);
  T_trigger t_trigger_1 (.T(1'b1), .C(C_out), .reset_0(and_1_out), .reset_1(and_2_out), .Q(x0));  // open: NQ
  or or_1 (or_1_out, reset, and_2_out);
  not not_2 (not_2_out, x0);
  and and_2 (and_2_out, x3, x2, x1, x0);
  not not_3 (not_3_out, x1);
  T_trigger t_trigger_2 (.T(not_2_out), .C(C_out), .reset_0(or_1_out), .Q(x1));  // open: reset_1, NQ
  and and_3 (and_3_out, reset, not_4_out);
  not not_4 (not_4_out, and_2_out);
  and and_4 (and_4_out, not_2_out, not_3_out);
  and and_5 (and_5_out, reset, not_6_out);
  not not_5 (not_5_out, x2);
  T_trigger t_trigger_3 (.T(and_4_out), .C(C_out), .reset_0(and_3_out), .reset_1(and_2_out), .Q(x2));  // open: NQ
  not not_6 (not_6_out, and_2_out);
  and and_6 (and_6_out, not_5_out, not_2_out, not_3_out);
  Hex_Digit_Display hex_digit_display_1 (.value({x3, x2, x1, x0}));  // open: dp
  T_trigger t_trigger_4 (.T(and_6_out), .C(C_out), .reset_0(and_5_out), .reset_1(and_2_out), .Q(x3));  // open: NQ
endmodule

module sqrt (
  input  [7:0] in_1,
  output [3:0] out_2
);

  wire [7:0] mul2_1_out_2, mul2_2_out_2, mul2_3_out_2, mul2_4_out_2;

  mul2 mul2_1 (.in_1(4'b1000), .out_2(mul2_1_out_2));
  mul2 mul2_2 (.in_1({out_2[3], 3'b100}), .out_2(mul2_2_out_2));
  mul2 mul2_3 (.in_1({out_2[3:2], 2'b10}), .out_2(mul2_3_out_2));
  mul2 mul2_4 (.in_1({out_2[3:1], 1'b1}), .out_2(mul2_4_out_2));
  less_or_equal8 less_or_equal8_1 (.A(mul2_1_out_2), .B(in_1), .out_3(out_2[3]));
  less_or_equal8 less_or_equal8_2 (.A(mul2_2_out_2), .B(in_1), .out_3(out_2[2]));
  less_or_equal8 less_or_equal8_3 (.A(mul2_3_out_2), .B(in_1), .out_3(out_2[1]));
  less_or_equal8 less_or_equal8_4 (.A(mul2_4_out_2), .B(in_1), .out_3(out_2[0]));
endmodule

module mul2 (
  input  [3:0] in_1,
  output [7:0] out_2
);

  wire and_1_out, and_2_out, and_3_out, and_4_out, and_5_out, and_6_out, and_7_out, and_8_out, and_9_out,
       and_10_out, and_11_out, and_12_out, and_13_out, and_14_out, and_15_out, fulladder_2_cout,
       fulladder_2_s, fulladder_3_cout, fulladder_4_cout, fulladder_4_s, fulladder_5_cout, fulladder_5_s,
       fulladder_6_cout, fulladder_7_cout, fulladder_7_s, fulladder_8_cout, fulladder_8_s, fulladder_9_cout,
       fulladder_10_cout, fulladder_10_s, fulladder_11_cout, fulladder_12_cout;

  and and_1 (and_1_out, in_1[3], in_1[2]);
  and and_2 (and_2_out, in_1[3], in_1[3]);
  fullAdder fulladder_1 (.A(and_2_out), .B(fulladder_2_cout), .Cin(fulladder_3_cout), .S(out_2[6]), .Cout(out_2[7]));
  fullAdder fulladder_2 (
    .A(fulladder_4_cout), .B(and_1_out), .Cin(fulladder_5_cout), .S(fulladder_2_s), .Cout(fulladder_2_cout));
  and and_3 (and_3_out, in_1[2], in_1[3]);
  fullAdder fulladder_3 (
    .A(and_3_out), .B(fulladder_2_s), .Cin(fulladder_6_cout), .S(out_2[5]), .Cout(fulladder_3_cout));
  fullAdder fulladder_4 (.A(1'b0), .B(and_6_out), .Cin(fulladder_7_cout), .S(fulladder_4_s), .Cout(fulladder_4_cout));
  and and_4 (and_4_out, in_1[2], in_1[2]);
  fullAdder fulladder_5 (
    .A(fulladder_4_s), .B(and_4_out), .Cin(fulladder_8_cout), .S(fulladder_5_s), .Cout(fulladder_5_cout));
  fullAdder fulladder_6 (
    .A(and_8_out), .B(fulladder_5_s), .Cin(fulladder_9_cout), .S(out_2[4]), .Cout(fulladder_6_cout));
  and and_5 (and_5_out, in_1[3], in_1[0]);
  and and_6 (and_6_out, in_1[3], in_1[1]);
  fullAdder fulladder_7 (
    .A(and_10_out), .B(and_5_out), .Cin(fulladder_10_cout), .S(fulladder_7_s), .Cout(fulladder_7_cout));
  and and_7 (and_7_out, in_1[1], in_1[2]);
  fullAdder fulladder_8 (
    .A(fulladder_7_s), .B(and_7_out), .Cin(fulladder_11_cout), .S(fulladder_8_s), .Cout(fulladder_8_cout));
  and and_8 (and_8_out, in_1[1], in_1[3]);
  fullAdder fulladder_9 (.A(and_13_out), .B(fulladder_8_s), .Cin(1'b0), .S(out_2[3]), .Cout(fulladder_9_cout));
  and and_9 (and_9_out, in_1[2], in_1[0]);
  and and_10 (and_10_out, in_1[2], in_1[1]);
  and and_11 (and_11_out, in_1[1], in_1[1]);
  fullAdder fulladder_10 (
    .A(and_11_out), .B(and_9_out), .Cin(fulladder_12_cout), .S(fulladder_10_s), .Cout(fulladder_10_cout));
  and and_12 (and_12_out, in_1[0], in_1[2]);
  fullAdder fulladder_11 (.A(fulladder_10_s), .B(and_12_out), .Cin(1'b0), .S(out_2[2]), .Cout(fulladder_11_cout));
  and and_13 (and_13_out, in_1[0], in_1[3]);
  and and_14 (and_14_out, in_1[1], in_1[0]);
  and and_15 (and_15_out, in_1[0], in_1[1]);
  and and_16 (out_2[0], in_1[0], in_1[0]);
  fullAdder fulladder_12 (.A(and_15_out), .B(and_14_out), .Cin(1'b0), .S(out_2[1]), .Cout(fulladder_12_cout));
endmodule

module fullAdder (
  input  A,
  input  B,
  input  Cin,
  output S,
  output Cout
);

  wire and_1_out, and_2_out, xor_1_out;

  xor xor_1 (xor_1_out, A, B);
  xor xor_2 (S, xor_1_out, Cin);
  and and_1 (and_1_out, xor_1_out, Cin);
  and and_2 (and_2_out, A, B);
  or or_1 (Cout, and_1_out, and_2_out);
endmodule

module less_or_equal8 (
  input  [7:0] A,
  input  [7:0] B,
  output out_3
);

  wire and_1_out, and_2_out, and_3_out, and_4_out, and_5_out, and_6_out, and_7_out, and_8_out, and_9_out,
       and_10_out, and_11_out, and_12_out, and_13_out, and_14_out, less_or_equal_1_equal,
       less_or_equal_1_less, less_or_equal_2_equal, less_or_equal_2_less, less_or_equal_3_equal,
       less_or_equal_3_less, less_or_equal_4_equal, less_or_equal_4_less, less_or_equal_5_equal,
       less_or_equal_5_less, less_or_equal_6_equal, less_or_equal_6_less, less_or_equal_7_equal,
       less_or_equal_7_less, less_or_equal_8_equal, less_or_equal_8_less, or_1_out, or_2_out, or_3_out,
       or_4_out, or_5_out, or_6_out, or_7_out;

  less_or_equal less_or_equal_1 (.A(A[7]), .B(B[7]), .less(less_or_equal_1_less), .equal(less_or_equal_1_equal));
  less_or_equal less_or_equal_2 (.A(A[6]), .B(B[6]), .less(less_or_equal_2_less), .equal(less_or_equal_2_equal));
  less_or_equal less_or_equal_3 (.A(A[5]), .B(B[5]), .less(less_or_equal_3_less), .equal(less_or_equal_3_equal));
  less_or_equal less_or_equal_4 (.A(A[4]), .B(B[4]), .less(less_or_equal_4_less), .equal(less_or_equal_4_equal));
  less_or_equal less_or_equal_5 (.A(A[3]), .B(B[3]), .less(less_or_equal_5_less), .equal(less_or_equal_5_equal));
  less_or_equal less_or_equal_6 (.A(A[2]), .B(B[2]), .less(less_or_equal_6_less), .equal(less_or_equal_6_equal));
  less_or_equal less_or_equal_7 (.A(A[1]), .B(B[1]), .less(less_or_equal_7_less), .equal(less_or_equal_7_equal));
  less_or_equal less_or_equal_8 (.A(A[0]), .B(B[0]), .less(less_or_equal_8_less), .equal(less_or_equal_8_equal));
  and and_1 (and_1_out, less_or_equal_1_equal, less_or_equal_2_equal);
  and and_2 (and_2_out, and_1_out, less_or_equal_3_equal);
  and and_3 (and_3_out, and_2_out, less_or_equal_4_equal);
  and and_4 (and_4_out, and_3_out, less_or_equal_5_equal);
  and and_5 (and_5_out, and_4_out, less_or_equal_6_equal);
  and and_6 (and_6_out, and_5_out, less_or_equal_7_equal);
  and and_7 (and_7_out, and_6_out, less_or_equal_8_equal);
  and and_8 (and_8_out, less_or_equal_1_equal, less_or_equal_2_less);
  and and_9 (and_9_out, and_1_out, less_or_equal_3_less);
  and and_10 (and_10_out, and_2_out, less_or_equal_4_less);
  and and_11 (and_11_out, and_3_out, less_or_equal_5_less);
  and and_12 (and_12_out, and_4_out, less_or_equal_6_less);
  and and_13 (and_13_out, and_5_out, less_or_equal_7_less);
  and and_14 (and_14_out, and_6_out, less_or_equal_8_less);
  or or_1 (or_1_out, and_8_out, less_or_equal_1_less);
  or or_2 (or_2_out, and_9_out, or_1_out);
  or or_3 (or_3_out, and_10_out, or_2_out);
  or or_4 (or_4_out, and_11_out, or_3_out);
  or or_5 (or_5_out, and_12_out, or_4_out);
  or or_6 (or_6_out, and_13_out, or_5_out);
  or or_7 (or_7_out, and_14_out, or_6_out);
  or or_8 (out_3, and_7_out, or_7_out);
endmodule

module less_or_equal (
  input  A,
  input  B,
  output less,
  output equal
);

  wire not_1_out;

  not not_1 (not_1_out, A);
  and and_1 (less, not_1_out, B);
  xnor xnor_1 (equal, A, B);
endmodule
